# Fritzing sketch Electronics box (saved by Fritzing 0.9.3b)
breadboards: 1

parts:
  Stepper_driver = IC, DIP package, 16 pins [chip_label="Polulu md20b"]
  Stepper_driver_2 = IC, DIP package, 16 pins [chip_label="Polulu md20b"]
  R1 = Resistor [tolerance=±5% resistance=330 package=THT]
  R2 = Resistor [tolerance=±5% resistance=330 package=THT]
  Fathom-X_Tether_Interface_Board = IC, DIP package, 4 pins [chip_label="\nFathom-X Tether Interface Board"]
  S1 = Pushbutton [package=THT]
  S3 = Pushbutton [package=THT]
  Camera_servo = Basic Servo
  LED_lights = IC, SIP package, 3 pins [chip_label="Lumen subsea light"]
  Teensy1 = Teensy 4.0
  Teensy2 = Teensy 4.0
  Raspberry_Pi_4 = Raspberry Pi 2
  Pressure_sensor1 = IC, DIP package, 4 pins [chip_label=MS5837-30BA1]
  Adafruit_9dof_IMU1 = IC, DIP package, 4 pins [chip_label=IMU]
  Echo_sounder1 = IC, DIP package, 4 pins [chip_label=PING-SONAR]
  Leak_sensor = IC, DIP package, 4 pins [chip_label="SOS Leak Sensor"]
  Stepper_motor_1 = Stepper Motor - Bipolar
  Stepper_motor_2 = Stepper Motor - Bipolar

nets:
  5V custom PCB: Stepper_driver.pin5, Stepper_driver.pin6, Stepper_driver_2.pin5, Stepper_driver_2.pin6, S1.leg1, S3.leg1
  N1: Stepper_driver.pin7, Teensy1.pin_8
  N2: Stepper_driver.pin8, Teensy1.pin_7
  GND(5V): Stepper_driver.pin9, Stepper_driver_2.pin9
  N3: Stepper_driver.pin11, Stepper_motor_1.D
  N4: Stepper_driver.pin12, Stepper_motor_1.B
  N5: Stepper_driver.pin13, Stepper_motor_1.C
  N6: Stepper_driver.pin14, Stepper_motor_1.A
  GND(12V) custom PCB: Stepper_driver.pin15, Stepper_driver_2.pin15
  12V custom PCB: Stepper_driver.pin16, Stepper_driver_2.pin16
  N7: Stepper_driver_2.pin7, Teensy1.pin_5
  N8: Stepper_driver_2.pin8, Teensy1.pin_4
  N9: Stepper_driver_2.pin11, Stepper_motor_2.D
  N10: Stepper_driver_2.pin12, Stepper_motor_2.B
  N11: Stepper_driver_2.pin13, Stepper_motor_2.C
  N12: Stepper_driver_2.pin14, Stepper_motor_2.A
  N13: R1.Pin_0, S1.leg0, Teensy1.pin_9
  GND: R1.Pin_1, R2.Pin_1, Pressure_sensor1.pin3, Adafruit_9dof_IMU1.pin3, Echo_sounder1.pin2, Leak_sensor.pin2
  N14: R2.Pin_0, S3.leg0, Teensy1.pin_6
  Theter cable - (white): Fathom-X_Tether_Interface_Board.pin1
  Theter cable - (Blue): Fathom-X_Tether_Interface_Board.pin2
  GND Custom PCB: Fathom-X_Tether_Interface_Board.pin3
  12V Custom PCB: Fathom-X_Tether_Interface_Board.pin4, LED_lights.pin2
  GND(5V) Custom PCB: Camera_servo.gnd, Teensy1.pin_17, Teensy1.pin_32, Teensy2.pin_17, Teensy2.pin_32, Raspberry_Pi_4.GND
  5V: Camera_servo.vcc, Teensy1.pin33, Teensy2.pin33, Raspberry_Pi_4.5V, Pressure_sensor1.pin4, Adafruit_9dof_IMU1.pin4, Echo_sounder1.pin1
  N15: Camera_servo.pulse, Raspberry_Pi_4.GPIO16
  GND(12V) Custom PCB: LED_lights.pin1
  N16: LED_lights.pin3, Raspberry_Pi_4.GPIO20
  N17: Teensy1.pin_2, Raspberry_Pi_4.GPIO4
  N18: Teensy1.pin_3, Raspberry_Pi_4.GPIO5
  N19: Teensy2.pin_2, Raspberry_Pi_4.GPIO14
  N20: Teensy2.pin_3, Raspberry_Pi_4.GPIO15
  N21: Teensy2.pin_4, Leak_sensor.pin3
  N22: Teensy2.pin_9, Echo_sounder1.pin4
  N23: Teensy2.pin_10, Echo_sounder1.pin3
  N24: Teensy2.pin_16, Teensy2.pin_31, Leak_sensor.pin1
  N25: Teensy2.pin_25, Pressure_sensor1.pin1, Adafruit_9dof_IMU1.pin1
  N26: Teensy2.pin_26, Pressure_sensor1.pin2, Adafruit_9dof_IMU1.pin2

custom parts:
  Teensy 4.0: The Teensy is a complete USB-based microcontoller development system, in a very small footprint, capable of implementing many types of projects. All programming is done via the USB port. No special programmer is needed, only a standard micro-USB cable and a PC or Macintosh with a USB port.
